// Logisim project b23cs1004_alu.circ as structural Verilog: 1 circuit, main circuit main
module main (
  input  [31:0] Input1_32bit,
  input  [31:0] Input2_32bit,
  input  [3:0] Selector_4bit,
  output Zero,
  output [31:0] ALU_Result,
  output Overflow
);

  wire comparator_1_lt;
  wire [31:0] adder_1_out, and_1_out, bit_extender_1_out, or_1_out, subtractor_1_out;

  Adder #(.width(32)) adder_1 (.a(Input1_32bit), .b(Input2_32bit), .out(adder_1_out), .cout(Overflow));  // open: cin
  Subtractor #(.width(32)) subtractor_1 (
    .a(Input1_32bit), .b(Input2_32bit), .out(subtractor_1_out));  // open: bin, bout
  assign or_1_out = Input1_32bit | Input2_32bit;  // OR_Gate or_1, 32 bits wide
  assign and_1_out = Input1_32bit & Input2_32bit;  // AND_Gate and_1, 32 bits wide
  Comparator #(.width(32)) comparator_1 (.a(Input1_32bit), .b(Input2_32bit), .lt(comparator_1_lt));  // open: gt, eq
  assign bit_extender_1_out = {{31{1'b0}}, comparator_1_lt};  // Bit_Extender bit_extender_1
  Comparator #(.width(32)) comparator_2 (.a({32{1'b0}}), .b(ALU_Result), .eq(Zero));  // open: gt, lt
  Multiplexer #(.select(4), .width(32), .enable("false")) multiplexer_1 (
    .in0(and_1_out), .in1(or_1_out), .in2(adder_1_out), .in6(subtractor_1_out), .in7(bit_extender_1_out),
    .out(ALU_Result), .sel(Selector_4bit));  // open: in3, in4, in5, in8, in9, in10, in11, in12, in13, in14, in15
endmodule
