// Logisim project b23cs1004_alu_control.circ as structural Verilog: 1 circuit, main circuit main
module main (
  input  [5:0] Funct_Field,
  input  [1:0] ALUOp,
  output [3:0] ALU_Input
);

  wire [4:0] bit_extender_1_out;
  wire [5:0] multiplexer_1_out;

  Multiplexer #(.select(2), .width(6), .enable("false")) multiplexer_1 (
    .in0(6'b100000), .in1(6'b100010), .in2(Funct_Field), .out(multiplexer_1_out), .sel(ALUOp));  // open: in3
  Bit_Extender #(.in_width(6), .out_width(5)) bit_extender_1 (.in(multiplexer_1_out), .out(bit_extender_1_out));
  Multiplexer #(.select(5), .width(4), .enable("false")) multiplexer_2 (
    .in0(4'b0010), .in2(4'b0110), .in4(4'b0000), .in5(4'b0001), .in10(4'b0111), .out(ALU_Input),
    .sel(bit_extender_1_out));  // open: in1, in3, in6, in7, in8, in9, in11, in12, in13, in14, in15, in16, in17, in18, in19, in20, in21, in22, in23, in24, in25, in26, in27, in28, in29, in30, in31

  // Notes on the sheet:
  //   for lw,sw
  //   for R-type
  //   for branching
endmodule
