// Logisim project b23cs1004_control_unit.circ as structural Verilog: 1 circuit, main circuit main
module main (
  input  [5:0] OpCode,
  output RegDst,
  output Branch,
  output MemRead,
  output MemtoReg,
  output [1:0] ALUop,
  output MemWrite,
  output ALUSrc,
  output RegWrite,
  output Jump
);

  wire addi_out;

  and R_Format (ALUop[1], ~OpCode[5], ~OpCode[4], ~OpCode[3], ~OpCode[2], ~OpCode[1], ~OpCode[0]);  // AND_Gate
  and sw (MemWrite, OpCode[5], ~OpCode[4], OpCode[3], ~OpCode[2], OpCode[1], OpCode[0]);  // AND_Gate
  and lw (MemRead, OpCode[5], ~OpCode[4], ~OpCode[3], ~OpCode[2], OpCode[1], OpCode[0]);  // AND_Gate
  and beq (ALUop[0], ~OpCode[5], ~OpCode[4], ~OpCode[3], OpCode[2], ~OpCode[1], ~OpCode[0]);  // AND_Gate
  and j_type (Jump, ~OpCode[5], ~OpCode[4], ~OpCode[3], ~OpCode[2], OpCode[1], ~OpCode[0]);  // AND_Gate
  and addi (addi_out, ~OpCode[5], ~OpCode[4], OpCode[3], ~OpCode[2], ~OpCode[1], ~OpCode[0]);  // AND_Gate
  or or_1 (ALUSrc, MemWrite, addi_out, MemRead);
  or or_2 (RegWrite, MemRead, addi_out, ALUop[1]);

  assign Branch = ALUop[0];
  assign MemtoReg = MemRead;
  assign RegDst = ALUop[1];
endmodule
