// Logisim project b23cs1004_data_memory.circ as structural Verilog: 1 circuit, main circuit main
module main (
  input  [31:0] Address,
  input  [31:0] Write_data,
  input  MemWrite,
  input  Clock,
  input  MemRead,
  output [31:0] Read_Data
);

  wire [23:0] bit_extender_1_out;

  Bit_Extender #(.in_width(32), .out_width(24)) bit_extender_1 (.in(Address), .out(bit_extender_1_out));
  RAM #(.addrWidth(24), .dataWidth(32), .bus("separate")) ram_1 (
    .addr(bit_extender_1_out), .din(Write_data), .data(Read_Data), .str(MemWrite), .sel(1'b1), .clk(Clock),
    .ld(MemRead));  // open: clr
endmodule
