// Logisim project b23cs1004_instruction_memory.circ as structural Verilog: 1 circuit, main circuit main
module main (
  input  [31:0] InstructionAddress,
  input  clock,
  input  Load_Instruction,
  output [31:0] Instruction
);

  wire [23:0] bit_extender_1_out;

  Bit_Extender #(.in_width(32), .out_width(24)) bit_extender_1 (.in(InstructionAddress), .out(bit_extender_1_out));
  RAM #(.addrWidth(24), .dataWidth(32)) ram_1 (
    .addr(bit_extender_1_out), .data(Instruction), .sel(1'b1), .clk(clock), .ld(Load_Instruction));  // open: clr
endmodule
