// Logisim project b23cs1004_main.circ as structural Verilog: 7 circuits, main circuit main
// alu
module main (
  input  in_1,
  input  Reset_PC,
  output [31:0] out_3
);

  wire ALUSrc, and_2_out, Branch, clk, clk_out, Jump, MemRead, MemtoReg, MemWrite, overflow, RegDst,
       RegWrite, Zero;
  wire [1:0] ALUOp;
  wire [3:0] ALU_Control_alu_input;
  wire [4:0] multiplexer_1_out;
  wire [31:0] adder_1_out, adder_2_out, ALU_alu_result, bit_extender_1_out, Data_Memory_read_data,
       Instruction_Memory_instruction, multiplexer_2_out, PC, Program_Counter_q, reg_file_read_data1,
       reg_file_read_data2, shifter_1_out;

  Clock u_clk (.out(clk_out));
  Register #(.width(32)) Program_Counter (.D(PC), .Q(Program_Counter_q), .clk(clk), .clr(Reset_PC));  // open: en
  and and_1 (clk, clk_out, in_1);
  Instruction_Memory Instruction_Memory (
    .InstructionAddress(Program_Counter_q), .Load_Instruction(in_1),
    .Instruction(Instruction_Memory_instruction));  // open: clock
  ControlUnit control (
    .OpCode(Instruction_Memory_instruction[31:26]), .RegDst(RegDst), .Branch(Branch), .MemRead(MemRead),
    .MemtoReg(MemtoReg), .ALUop(ALUOp), .MemWrite(MemWrite), .ALUSrc(ALUSrc), .RegWrite(RegWrite), .Jump(Jump));
  Multiplexer #(.width(5), .enable("false")) multiplexer_1 (
    .in0(Instruction_Memory_instruction[20:16]), .in1(Instruction_Memory_instruction[15:11]),
    .out(multiplexer_1_out), .sel(RegDst));
  Adder #(.width(32)) adder_1 (.a(Program_Counter_q), .b(32'h4), .out(adder_1_out));  // open: cin, cout
  registers reg_file (
    .Write_Data(out_3), .RegWrite(RegWrite), .Write_Reg(multiplexer_1_out), .clock(clk),
    .Read_data1(reg_file_read_data1), .Read_Reg1(Instruction_Memory_instruction[25:21]),
    .Read_Data2(reg_file_read_data2), .Read_Reg2(Instruction_Memory_instruction[20:16]));
  assign bit_extender_1_out = {{16{1'b0}}, Instruction_Memory_instruction[15:0]};  // Bit_Extender bit_extender_1
  Multiplexer #(.width(32), .enable("false")) multiplexer_2 (
    .in0(reg_file_read_data2), .in1(bit_extender_1_out), .out(multiplexer_2_out), .sel(ALUSrc));
  Shifter #(.width(32)) shifter_1 (.in(bit_extender_1_out), .\dist (5'b00010), .out(shifter_1_out));
  ALU_Control ALU_Control (
    .Funct_Field(Instruction_Memory_instruction[5:0]), .ALUOp(ALUOp), .ALU_Input(ALU_Control_alu_input));
  Adder #(.width(32)) adder_2 (.a(adder_1_out), .b(shifter_1_out), .out(adder_2_out));  // open: cin, cout
  ALU ALU (
    .Input1_32bit(reg_file_read_data1), .Input2_32bit(multiplexer_2_out),
    .Selector_4bit(ALU_Control_alu_input), .Zero(Zero), .ALU_Result(ALU_alu_result), .Overflow(overflow));
  Multiplexer #(.width(32), .enable("false")) multiplexer_3 (
    .in0(adder_1_out), .in1(adder_2_out), .out(PC), .sel(and_2_out));
  and and_2 (and_2_out, Branch, Zero);
  Data_Memory Data_Memory (
    .Address(ALU_alu_result), .Write_data(reg_file_read_data2), .MemWrite(MemWrite), .Clock(clk),
    .MemRead(MemRead), .Read_Data(Data_Memory_read_data));
  Multiplexer #(.width(32), .enable("false")) multiplexer_4 (
    .in0(ALU_alu_result), .in1(Data_Memory_read_data), .out(out_3), .sel(MemtoReg));

  // Other names for the same wires on the sheet: Write_Data[31:0] = out_3
endmodule

module registers (
  input  [31:0] Write_Data,
  input  [4:0] Read_Reg1,
  input  RegWrite,
  input  [4:0] Write_Reg,
  input  [4:0] Read_Reg2,
  input  clock,
  output [31:0] Read_data1,
  output [31:0] Read_Data2
);

  wire decoder_1_out1, decoder_1_out2, decoder_1_out3, decoder_1_out4, decoder_1_out5, decoder_1_out6,
       decoder_1_out7, decoder_1_out8, decoder_1_out9, decoder_1_out10, decoder_1_out11, decoder_1_out12,
       decoder_1_out13, decoder_1_out14, decoder_1_out15, decoder_1_out16, decoder_1_out17, decoder_1_out18,
       decoder_1_out19, decoder_1_out20, decoder_1_out21, decoder_1_out22, decoder_1_out23, decoder_1_out24,
       decoder_1_out25, decoder_1_out26, decoder_1_out27, decoder_1_out28, decoder_1_out29, decoder_1_out30,
       decoder_1_out31;
  wire [31:0] a0_q, a1_q, a2_q, a3_q, at_q, fp_q, gp_q, k0_q, k1_q, ra_q, s0_q, s1_q, s2_q, s3_q, s4_q, s5_q,
       s6_q, s7_q, sp_q, t0_q, t1_q, t2_q, t3_q, t4_q, t5_q, t6_q, t7_q, t8_q, t9_q, v0_q, v1_q;

  Decoder #(.select(5)) decoder_1 (
    .out1(decoder_1_out1), .out2(decoder_1_out2), .out3(decoder_1_out3), .out4(decoder_1_out4),
    .out5(decoder_1_out5), .out6(decoder_1_out6), .out7(decoder_1_out7), .out8(decoder_1_out8),
    .out9(decoder_1_out9), .out10(decoder_1_out10), .out11(decoder_1_out11), .out12(decoder_1_out12),
    .out13(decoder_1_out13), .out14(decoder_1_out14), .out15(decoder_1_out15), .out16(decoder_1_out16),
    .out17(decoder_1_out17), .out18(decoder_1_out18), .out19(decoder_1_out19), .out20(decoder_1_out20),
    .out21(decoder_1_out21), .out22(decoder_1_out22), .out23(decoder_1_out23), .out24(decoder_1_out24),
    .out25(decoder_1_out25), .out26(decoder_1_out26), .out27(decoder_1_out27), .out28(decoder_1_out28),
    .out29(decoder_1_out29), .out30(decoder_1_out30), .out31(decoder_1_out31), .sel(Write_Reg), .en(RegWrite));  // open: out0
  Register #(.width(32)) at (.D(Write_Data), .en(decoder_1_out1), .Q(at_q), .clk(clock));  // open: clr
  Register #(.width(32)) v0 (.D(Write_Data), .en(decoder_1_out2), .Q(v0_q), .clk(clock));  // open: clr
  Register #(.width(32)) v1 (.D(Write_Data), .en(decoder_1_out3), .Q(v1_q), .clk(clock));  // open: clr
  Register #(.width(32)) a0 (.D(Write_Data), .en(decoder_1_out4), .Q(a0_q), .clk(clock));  // open: clr
  Register #(.width(32)) a1 (.D(Write_Data), .en(decoder_1_out5), .Q(a1_q), .clk(clock));  // open: clr
  Register #(.width(32)) a2 (.D(Write_Data), .en(decoder_1_out6), .Q(a2_q), .clk(clock));  // open: clr
  Register #(.width(32)) a3 (.D(Write_Data), .en(decoder_1_out7), .Q(a3_q), .clk(clock));  // open: clr
  Register #(.width(32)) t0 (.D(Write_Data), .en(decoder_1_out8), .Q(t0_q), .clk(clock));  // open: clr
  Register #(.width(32)) t1 (.D(Write_Data), .en(decoder_1_out9), .Q(t1_q), .clk(clock));  // open: clr
  Register #(.width(32)) t2 (.D(Write_Data), .en(decoder_1_out10), .Q(t2_q), .clk(clock));  // open: clr
  Register #(.width(32)) t3 (.D(Write_Data), .en(decoder_1_out11), .Q(t3_q), .clk(clock));  // open: clr
  Register #(.width(32)) t4 (.D(Write_Data), .en(decoder_1_out12), .Q(t4_q), .clk(clock));  // open: clr
  Register #(.width(32)) t5 (.D(Write_Data), .en(decoder_1_out13), .Q(t5_q), .clk(clock));  // open: clr
  Register #(.width(32)) t6 (.D(Write_Data), .en(decoder_1_out14), .Q(t6_q), .clk(clock));  // open: clr
  Register #(.width(32)) t7 (.D(Write_Data), .en(decoder_1_out15), .Q(t7_q), .clk(clock));  // open: clr
  Register #(.width(32)) s0 (.D(Write_Data), .en(decoder_1_out16), .Q(s0_q), .clk(clock));  // open: clr
  Register #(.width(32)) s1 (.D(Write_Data), .en(decoder_1_out17), .Q(s1_q), .clk(clock));  // open: clr
  Register #(.width(32)) s2 (.D(Write_Data), .en(decoder_1_out18), .Q(s2_q), .clk(clock));  // open: clr
  Register #(.width(32)) s3 (.D(Write_Data), .en(decoder_1_out19), .Q(s3_q), .clk(clock));  // open: clr
  Register #(.width(32)) s4 (.D(Write_Data), .en(decoder_1_out20), .Q(s4_q), .clk(clock));  // open: clr
  Register #(.width(32)) s5 (.D(Write_Data), .en(decoder_1_out21), .Q(s5_q), .clk(clock));  // open: clr
  Register #(.width(32)) s6 (.D(Write_Data), .en(decoder_1_out22), .Q(s6_q), .clk(clock));  // open: clr
  Register #(.width(32)) s7 (.D(Write_Data), .en(decoder_1_out23), .Q(s7_q), .clk(clock));  // open: clr
  Register #(.width(32)) t8 (.D(Write_Data), .en(decoder_1_out24), .Q(t8_q), .clk(clock));  // open: clr
  Register #(.width(32)) t9 (.D(Write_Data), .en(decoder_1_out25), .Q(t9_q), .clk(clock));  // open: clr
  Register #(.width(32)) k0 (.D(Write_Data), .en(decoder_1_out26), .Q(k0_q), .clk(clock));  // open: clr
  Register #(.width(32)) k1 (.D(Write_Data), .en(decoder_1_out27), .Q(k1_q), .clk(clock));  // open: clr
  Register #(.width(32)) gp (.D(Write_Data), .en(decoder_1_out28), .Q(gp_q), .clk(clock));  // open: clr
  Register #(.width(32)) sp (.D(Write_Data), .en(decoder_1_out29), .Q(sp_q), .clk(clock));  // open: clr
  Register #(.width(32)) fp (.D(Write_Data), .en(decoder_1_out30), .Q(fp_q), .clk(clock));  // open: clr
  Register #(.width(32)) ra (.D(Write_Data), .en(decoder_1_out31), .Q(ra_q), .clk(clock));  // open: clr
  Multiplexer #(.select(5), .width(32)) multiplexer_1 (
    .in0({32{1'b0}}), .in1(at_q), .in2(v0_q), .in3(v1_q), .in4(a0_q), .in5(a1_q), .in6(a2_q), .in7(a3_q),
    .in8(t0_q), .in9(t1_q), .in10(t2_q), .in11(t3_q), .in12(t4_q), .in13(t5_q), .in14(t6_q), .in15(t7_q),
    .in16(s0_q), .in17(s1_q), .in18(s2_q), .in19(s3_q), .in20(s4_q), .in21(s5_q), .in22(s6_q), .in23(s7_q),
    .in24(t8_q), .in25(t9_q), .in26(k0_q), .in27(k1_q), .in28(gp_q), .in29(sp_q), .in30(fp_q), .in31(ra_q),
    .out(Read_data1), .sel(Read_Reg1), .en(1'b1));
  Multiplexer #(.select(5), .width(32)) multiplexer_2 (
    .in0({32{1'b0}}), .in1(at_q), .in2(v0_q), .in3(v1_q), .in4(a0_q), .in5(a1_q), .in6(a2_q), .in7(a3_q),
    .in8(t0_q), .in9(t1_q), .in10(t2_q), .in11(t3_q), .in12(t4_q), .in13(t5_q), .in14(t6_q), .in15(t7_q),
    .in16(s0_q), .in17(s1_q), .in18(s2_q), .in19(s3_q), .in20(s4_q), .in21(s5_q), .in22(s6_q), .in23(s7_q),
    .in24(t8_q), .in25(t9_q), .in26(k0_q), .in27(k1_q), .in28(gp_q), .in29(sp_q), .in30(fp_q), .in31(ra_q),
    .out(Read_Data2), .sel(Read_Reg2), .en(1'b1));
endmodule

module ControlUnit (
  input  [5:0] OpCode,
  output RegDst,
  output Branch,
  output MemRead,
  output MemtoReg,
  output [1:0] ALUop,
  output MemWrite,
  output ALUSrc,
  output RegWrite,
  output Jump
);

  wire addi_out;

  and R_Format (ALUop[1], ~OpCode[5], ~OpCode[4], ~OpCode[3], ~OpCode[2], ~OpCode[1], ~OpCode[0]);  // AND_Gate
  and sw (MemWrite, OpCode[5], ~OpCode[4], OpCode[3], ~OpCode[2], OpCode[1], OpCode[0]);  // AND_Gate
  and lw (MemRead, OpCode[5], ~OpCode[4], ~OpCode[3], ~OpCode[2], OpCode[1], OpCode[0]);  // AND_Gate
  and beq (ALUop[0], ~OpCode[5], ~OpCode[4], ~OpCode[3], OpCode[2], ~OpCode[1], ~OpCode[0]);  // AND_Gate
  and j_type (Jump, ~OpCode[5], ~OpCode[4], ~OpCode[3], ~OpCode[2], OpCode[1], ~OpCode[0]);  // AND_Gate
  and addi (addi_out, ~OpCode[5], ~OpCode[4], OpCode[3], ~OpCode[2], ~OpCode[1], ~OpCode[0]);  // AND_Gate
  or or_1 (ALUSrc, MemWrite, addi_out, MemRead);
  or or_2 (RegWrite, MemRead, addi_out, ALUop[1]);

  assign Branch = ALUop[0];
  assign MemtoReg = MemRead;
  assign RegDst = ALUop[1];
endmodule

module ALU_Control (
  input  [5:0] Funct_Field,
  input  [1:0] ALUOp,
  output [3:0] ALU_Input
);

  wire [4:0] bit_extender_1_out;
  wire [5:0] multiplexer_1_out;

  Multiplexer #(.select(2), .width(6), .enable("false")) multiplexer_1 (
    .in0(6'b100000), .in1(6'b100010), .in2(Funct_Field), .out(multiplexer_1_out), .sel(ALUOp));  // open: in3
  Bit_Extender #(.in_width(6), .out_width(5)) bit_extender_1 (.in(multiplexer_1_out), .out(bit_extender_1_out));
  Multiplexer #(.select(5), .width(4), .enable("false")) multiplexer_2 (
    .in0(4'b0010), .in2(4'b0110), .in4(4'b0000), .in5(4'b0001), .in10(4'b0111), .out(ALU_Input),
    .sel(bit_extender_1_out));  // open: in1, in3, in6, in7, in8, in9, in11, in12, in13, in14, in15, in16, in17, in18, in19, in20, in21, in22, in23, in24, in25, in26, in27, in28, in29, in30, in31

  // Notes on the sheet:
  //   for lw,sw
  //   for R-type
  //   for branching
endmodule

module ALU (
  input  [31:0] Input1_32bit,
  input  [31:0] Input2_32bit,
  input  [3:0] Selector_4bit,
  output Zero,
  output [31:0] ALU_Result,
  output Overflow
);

  wire comparator_1_lt;
  wire [31:0] adder_1_out, and_1_out, bit_extender_1_out, or_1_out, subtractor_1_out;

  Adder #(.width(32)) adder_1 (.a(Input1_32bit), .b(Input2_32bit), .out(adder_1_out), .cout(Overflow));  // open: cin
  Subtractor #(.width(32)) subtractor_1 (
    .a(Input1_32bit), .b(Input2_32bit), .out(subtractor_1_out));  // open: bin, bout
  assign or_1_out = Input1_32bit | Input2_32bit;  // OR_Gate or_1, 32 bits wide
  assign and_1_out = Input1_32bit & Input2_32bit;  // AND_Gate and_1, 32 bits wide
  Comparator #(.width(32)) comparator_1 (.a(Input1_32bit), .b(Input2_32bit), .lt(comparator_1_lt));  // open: gt, eq
  assign bit_extender_1_out = {{31{1'b0}}, comparator_1_lt};  // Bit_Extender bit_extender_1
  Comparator #(.width(32)) comparator_2 (.a({32{1'b0}}), .b(ALU_Result), .eq(Zero));  // open: gt, lt
  Multiplexer #(.select(4), .width(32), .enable("false")) multiplexer_1 (
    .in0(and_1_out), .in1(or_1_out), .in2(adder_1_out), .in6(subtractor_1_out), .in7(bit_extender_1_out),
    .out(ALU_Result), .sel(Selector_4bit));  // open: in3, in4, in5, in8, in9, in10, in11, in12, in13, in14, in15
endmodule

module Instruction_Memory (
  input  [31:0] InstructionAddress,
  input  clock,
  input  Load_Instruction,
  output [31:0] Instruction
);

  wire [23:0] bit_extender_1_out;

  Bit_Extender #(.in_width(32), .out_width(24)) bit_extender_1 (.in(InstructionAddress), .out(bit_extender_1_out));
  RAM #(.addrWidth(24), .dataWidth(32)) ram_1 (
    .addr(bit_extender_1_out), .data(Instruction), .sel(1'b1), .clk(clock), .ld(Load_Instruction));  // open: clr
endmodule

module Data_Memory (
  input  [31:0] Address,
  input  [31:0] Write_data,
  input  MemWrite,
  input  Clock,
  input  MemRead,
  output [31:0] Read_Data
);

  wire [23:0] bit_extender_1_out;

  Bit_Extender #(.in_width(32), .out_width(24)) bit_extender_1 (.in(Address), .out(bit_extender_1_out));
  RAM #(.addrWidth(24), .dataWidth(32), .bus("separate")) ram_1 (
    .addr(bit_extender_1_out), .din(Write_data), .data(Read_Data), .str(MemWrite), .sel(1'b1), .clk(Clock),
    .ld(MemRead));  // open: clr
endmodule
